// Logisim project Projeto_Estrutura_Pedro_Pimentel (1).circ as structural Verilog: 8 circuits, main circuit main
module main (
  input  [3:0] A,
  input  [3:0] B,
  input  [2:0] \OPERAÇÕES ,
  output Overflow,
  output Overflow_2,
  output [3:0] out_6
);

  wire decoder_1_s0, decoder_1_s1, decoder_1_s2, decoder_1_s4;
  wire [3:0] add_4_1_out_5, sub_4_1_out_5;

  DECODER decoder_1 (
    .\OPERAÇÃO (\OPERAÇÕES ), .S0(decoder_1_s0), .S1(decoder_1_s1), .S2(decoder_1_s2), .S4(decoder_1_s4));  // open: S3, S5, S6, S7
  BUFFER buffer_1 (.in_2(decoder_1_s0), .S(out_6), .B(B));
  ADD_4 add_4_1 (.Vai_1(Overflow), .out_5(add_4_1_out_5), .in_1(A), .in_2(B), .Vem_1(1'b0));
  BUFFER buffer_2 (.in_2(decoder_1_s1), .S(out_6), .B(add_4_1_out_5));
  SUB_4 sub_4_1 (.in_2(B), .out_4(Overflow_2), .out_5(sub_4_1_out_5), .in_1(A), .in_3(1'b0));
  BUFFER buffer_3 (.in_2(decoder_1_s2), .S(out_6), .B(sub_4_1_out_5));
  BUFFER_INVERTIDO buffer_invertido_1 (.in_2(decoder_1_s4), .S(out_6), .B(B));
endmodule

module ADD_1 (
  input  A,
  input  B,
  input  Vem_1,
  output out_4,
  output out_5
);

  wire and_1_out, and_2_out, or_1_out, xor_1_out;

  xor xor_1 (xor_1_out, A, B);
  xor xor_2 (out_4, xor_1_out, Vem_1);
  or or_1 (or_1_out, B, Vem_1);
  and and_1 (and_1_out, B, Vem_1);
  and and_2 (and_2_out, or_1_out, A);
  or or_2 (out_5, and_2_out, and_1_out);
endmodule

module ADD_4 (
  input  [3:0] in_1,
  input  [3:0] in_2,
  input  Vem_1,
  output Vai_1,
  output [3:0] out_5
);

  wire add_1_2_out_5, add_1_3_out_5, add_1_4_out_5;

  ADD_1 add_1_1 (.A(in_1[3]), .B(in_2[3]), .Vem_1(add_1_2_out_5), .out_4(out_5[3]), .out_5(Vai_1));
  ADD_1 add_1_2 (.A(in_1[2]), .B(in_2[2]), .Vem_1(add_1_3_out_5), .out_4(out_5[2]), .out_5(add_1_2_out_5));
  ADD_1 add_1_3 (.A(in_1[1]), .B(in_2[1]), .Vem_1(add_1_4_out_5), .out_4(out_5[1]), .out_5(add_1_3_out_5));
  ADD_1 add_1_4 (.A(in_1[0]), .B(in_2[0]), .Vem_1(Vem_1), .out_4(out_5[0]), .out_5(add_1_4_out_5));
endmodule

module SUB_1 (
  input  A,
  input  B,
  input  Vem_1,
  output out_4,
  output out_5
);

  wire and_1_out, and_2_out, not_1_out, or_1_out, xor_1_out;

  not not_1 (not_1_out, A);
  xor xor_1 (xor_1_out, A, B);
  xor xor_2 (out_4, xor_1_out, Vem_1);
  or or_1 (or_1_out, B, Vem_1);
  and and_1 (and_1_out, B, Vem_1);
  and and_2 (and_2_out, or_1_out, not_1_out);
  or or_2 (out_5, and_2_out, and_1_out);
endmodule

module SUB_4 (
  input  [3:0] in_1,
  input  [3:0] in_2,
  input  in_3,
  output out_4,
  output [3:0] out_5
);

  wire sub_1_2_out_5, sub_1_3_out_5, sub_1_4_out_5;

  SUB_1 sub_1_1 (.A(in_1[3]), .B(in_2[3]), .Vem_1(sub_1_2_out_5), .out_4(out_5[3]), .out_5(out_4));
  SUB_1 sub_1_2 (.A(in_1[2]), .B(in_2[2]), .Vem_1(sub_1_3_out_5), .out_4(out_5[2]), .out_5(sub_1_2_out_5));
  SUB_1 sub_1_3 (.A(in_1[1]), .B(in_2[1]), .Vem_1(sub_1_4_out_5), .out_4(out_5[1]), .out_5(sub_1_3_out_5));
  SUB_1 sub_1_4 (.A(in_1[0]), .B(in_2[0]), .Vem_1(in_3), .out_4(out_5[0]), .out_5(sub_1_4_out_5));
endmodule

module BUFFER (
  input  [3:0] B,
  input  in_2,
  output [3:0] S
);

  assign S[3] = in_2 ? B[3] : 1'bz;  // Controlled_Buffer controlled_buffer_1
  assign S[2] = in_2 ? B[2] : 1'bz;  // Controlled_Buffer controlled_buffer_2
  assign S[1] = in_2 ? B[1] : 1'bz;  // Controlled_Buffer controlled_buffer_3
  assign S[0] = in_2 ? B[0] : 1'bz;  // Controlled_Buffer controlled_buffer_4
endmodule

module BUFFER_INVERTIDO (
  input  [3:0] B,
  input  in_2,
  output [3:0] S
);

  assign S[2] = in_2 ? ~B[2] : 1'bz;  // Controlled_Inverter controlled_inverter_1
  assign S[3] = in_2 ? ~B[3] : 1'bz;  // Controlled_Inverter controlled_inverter_2
  assign S[0] = in_2 ? ~B[0] : 1'bz;  // Controlled_Inverter controlled_inverter_3
  assign S[1] = in_2 ? ~B[1] : 1'bz;  // Controlled_Inverter controlled_inverter_4
endmodule

module DECODER (
  input  [2:0] \OPERAÇÃO ,
  output S0,
  output S1,
  output S2,
  output S3,
  output S4,
  output S5,
  output S6,
  output S7
);

  wire not_1_out, not_2_out, not_3_out, not_4_out, not_5_out, not_6_out, not_7_out, not_8_out, not_9_out,
       not_10_out, not_11_out, not_12_out;

  not not_1 (not_1_out, \OPERAÇÃO [0]);
  not not_2 (not_2_out, \OPERAÇÃO [1]);
  not not_3 (not_3_out, \OPERAÇÃO [2]);
  not not_4 (not_4_out, \OPERAÇÃO [0]);
  not not_5 (not_5_out, \OPERAÇÃO [1]);
  not not_6 (not_6_out, \OPERAÇÃO [0]);
  not not_7 (not_7_out, \OPERAÇÃO [2]);
  not not_8 (not_8_out, \OPERAÇÃO [0]);
  not not_9 (not_9_out, \OPERAÇÃO [1]);
  not not_10 (not_10_out, \OPERAÇÃO [2]);
  not not_11 (not_11_out, \OPERAÇÃO [2]);
  not not_12 (not_12_out, \OPERAÇÃO [2]);
  and and_1 (S7, \OPERAÇÃO [0], \OPERAÇÃO [1], \OPERAÇÃO [2]);
  and and_2 (S0, not_1_out, not_2_out, not_3_out);
  and and_3 (S1, not_4_out, not_5_out, \OPERAÇÃO [2]);
  and and_4 (S2, not_6_out, \OPERAÇÃO [1], not_7_out);
  and and_5 (S3, not_8_out, \OPERAÇÃO [1], \OPERAÇÃO [2]);
  and and_6 (S4, \OPERAÇÃO [0], not_9_out, not_10_out);
  and and_7 (S5, \OPERAÇÃO [2], not_11_out, \OPERAÇÃO [2]);
  and and_8 (S6, \OPERAÇÃO [0], \OPERAÇÃO [2], not_12_out);
endmodule
