// Logisim project Projeto_Estrutura_Pedro_Pimentel.circ as structural Verilog: 11 circuits, main circuit main
module main (
  input  D,
  input  [3:0] A,
  input  [3:0] B,
  input  [2:0] in_4,
  output Overflow,
  output [3:0] out_6,
  output Zero
);

  wire add_4_1_vai_1, and_1_out, and_2_out, decoder_1_s0, decoder_1_s1, decoder_1_s2, decoder_1_s3,
       decoder_1_s4, decoder_1_s5, decoder_1_s6, decoder_1_s7, not_1_out, sub_4_1_out_4;
  wire [3:0] add_4_1_out_5, buffer_5_s, or_4_1_s, \rotação_à_direita_1_abcd_2 ,
       \rotação_à_esquerda_1_abcd_2 , sub_4_1_out_5;

  and and_1 (and_1_out, add_4_1_vai_1, decoder_1_s1);
  or or_1 (Overflow, and_1_out, and_2_out);
  and and_2 (and_2_out, sub_4_1_out_4, decoder_1_s2);
  BUFFER buffer_1 (.in_2(decoder_1_s0), .S(out_6), .B(B));
  DECODER decoder_1 (
    .\OPERAÇÃO (in_4), .S0(decoder_1_s0), .S1(decoder_1_s1), .S2(decoder_1_s2), .S3(decoder_1_s3),
    .S4(decoder_1_s4), .S5(decoder_1_s5), .S6(decoder_1_s6), .S7(decoder_1_s7));
  nor nor_1 (Zero, decoder_1_s7, decoder_1_s6, out_6[0], out_6[1], out_6[2], out_6[3]);
  ADD_4 add_4_1 (.Vai_1(add_4_1_vai_1), .out_5(add_4_1_out_5), .in_1(A), .in_2(B), .Vem_1(1'b0));
  BUFFER buffer_2 (.in_2(decoder_1_s1), .S(out_6), .B(add_4_1_out_5));
  SUB_4 sub_4_1 (.in_2(B), .out_4(sub_4_1_out_4), .out_5(sub_4_1_out_5), .in_1(A), .in_3(1'b0));
  BUFFER buffer_3 (.in_2(decoder_1_s2), .S(out_6), .B(sub_4_1_out_5));
  OR_4 or_4_1 (.A(A), .S(or_4_1_s), .B(B));
  BUFFER buffer_4 (.in_2(decoder_1_s3), .S(out_6), .B(or_4_1_s));
  BUFFER_INVERTIDO buffer_invertido_1 (.in_2(decoder_1_s4), .S(out_6), .B(B));
  \ROTAÇÃO_À_DIREITA  \rotação_à_direita_1  (.ABCD(A), .XY(B[1:0]), .abcd_2(\rotação_à_direita_1_abcd_2 ));
  \ROTAÇÃO_À_ESQUERDA  \rotação_à_esquerda_1  (.ABCD(A), .XY(B[1:0]), .abcd_2(\rotação_à_esquerda_1_abcd_2 ));
  not not_1 (not_1_out, D);
  BUFFER buffer_5 (.in_2(D), .S(buffer_5_s), .B(\rotação_à_direita_1_abcd_2 ));
  BUFFER buffer_6 (.in_2(not_1_out), .S(buffer_5_s), .B(\rotação_à_esquerda_1_abcd_2 ));
  BUFFER buffer_7 (.in_2(decoder_1_s5), .S(out_6), .B(buffer_5_s));
endmodule

module ADD_1 (
  input  A,
  input  B,
  input  Vem_1,
  output out_4,
  output out_5
);

  wire and_1_out, and_2_out, or_1_out, xor_1_out;

  xor xor_1 (xor_1_out, A, B);
  xor xor_2 (out_4, xor_1_out, Vem_1);
  or or_1 (or_1_out, B, Vem_1);
  and and_1 (and_1_out, B, Vem_1);
  and and_2 (and_2_out, or_1_out, A);
  or or_2 (out_5, and_2_out, and_1_out);
endmodule

module ADD_4 (
  input  [3:0] in_1,
  input  [3:0] in_2,
  input  Vem_1,
  output Vai_1,
  output [3:0] out_5
);

  wire add_1_2_out_5, add_1_3_out_5, add_1_4_out_5;

  ADD_1 add_1_1 (.A(in_1[3]), .B(in_2[3]), .Vem_1(add_1_2_out_5), .out_4(out_5[3]), .out_5(Vai_1));
  ADD_1 add_1_2 (.A(in_1[2]), .B(in_2[2]), .Vem_1(add_1_3_out_5), .out_4(out_5[2]), .out_5(add_1_2_out_5));
  ADD_1 add_1_3 (.A(in_1[1]), .B(in_2[1]), .Vem_1(add_1_4_out_5), .out_4(out_5[1]), .out_5(add_1_3_out_5));
  ADD_1 add_1_4 (.A(in_1[0]), .B(in_2[0]), .Vem_1(Vem_1), .out_4(out_5[0]), .out_5(add_1_4_out_5));
endmodule

module SUB_1 (
  input  A,
  input  B,
  input  Vem_1,
  output out_4,
  output out_5
);

  wire and_1_out, and_2_out, not_1_out, or_1_out, xor_1_out;

  not not_1 (not_1_out, A);
  xor xor_1 (xor_1_out, A, B);
  xor xor_2 (out_4, xor_1_out, Vem_1);
  or or_1 (or_1_out, B, Vem_1);
  and and_1 (and_1_out, B, Vem_1);
  and and_2 (and_2_out, or_1_out, not_1_out);
  or or_2 (out_5, and_2_out, and_1_out);
endmodule

module SUB_4 (
  input  [3:0] in_1,
  input  [3:0] in_2,
  input  in_3,
  output out_4,
  output [3:0] out_5
);

  wire sub_1_2_out_5, sub_1_3_out_5, sub_1_4_out_5;

  SUB_1 sub_1_1 (.A(in_1[3]), .B(in_2[3]), .Vem_1(sub_1_2_out_5), .out_4(out_5[3]), .out_5(out_4));
  SUB_1 sub_1_2 (.A(in_1[2]), .B(in_2[2]), .Vem_1(sub_1_3_out_5), .out_4(out_5[2]), .out_5(sub_1_2_out_5));
  SUB_1 sub_1_3 (.A(in_1[1]), .B(in_2[1]), .Vem_1(sub_1_4_out_5), .out_4(out_5[1]), .out_5(sub_1_3_out_5));
  SUB_1 sub_1_4 (.A(in_1[0]), .B(in_2[0]), .Vem_1(in_3), .out_4(out_5[0]), .out_5(sub_1_4_out_5));
endmodule

module BUFFER (
  input  [3:0] B,
  input  in_2,
  output [3:0] S
);

  assign S[2] = in_2 ? B[2] : 1'bz;  // Controlled_Buffer controlled_buffer_1
  assign S[3] = in_2 ? B[3] : 1'bz;  // Controlled_Buffer controlled_buffer_2
  assign S[0] = in_2 ? B[0] : 1'bz;  // Controlled_Buffer controlled_buffer_3
  assign S[1] = in_2 ? B[1] : 1'bz;  // Controlled_Buffer controlled_buffer_4
endmodule

module BUFFER_INVERTIDO (
  input  [3:0] B,
  input  in_2,
  output [3:0] S
);

  assign S[2] = in_2 ? ~B[2] : 1'bz;  // Controlled_Inverter controlled_inverter_1
  assign S[3] = in_2 ? ~B[3] : 1'bz;  // Controlled_Inverter controlled_inverter_2
  assign S[0] = in_2 ? ~B[0] : 1'bz;  // Controlled_Inverter controlled_inverter_3
  assign S[1] = in_2 ? ~B[1] : 1'bz;  // Controlled_Inverter controlled_inverter_4
endmodule

module DECODER (
  input  [2:0] \OPERAÇÃO ,
  output S0,
  output S1,
  output S2,
  output S3,
  output S4,
  output S5,
  output S6,
  output S7
);

  wire not_1_out, not_2_out, not_3_out, not_4_out, not_5_out, not_6_out, not_7_out, not_8_out, not_9_out,
       not_10_out, not_11_out, not_12_out;

  not not_1 (not_1_out, \OPERAÇÃO [0]);
  not not_2 (not_2_out, \OPERAÇÃO [1]);
  not not_3 (not_3_out, \OPERAÇÃO [2]);
  not not_4 (not_4_out, \OPERAÇÃO [0]);
  not not_5 (not_5_out, \OPERAÇÃO [1]);
  not not_6 (not_6_out, \OPERAÇÃO [0]);
  not not_7 (not_7_out, \OPERAÇÃO [2]);
  not not_8 (not_8_out, \OPERAÇÃO [0]);
  not not_9 (not_9_out, \OPERAÇÃO [1]);
  not not_10 (not_10_out, \OPERAÇÃO [2]);
  not not_11 (not_11_out, \OPERAÇÃO [1]);
  not not_12 (not_12_out, \OPERAÇÃO [2]);
  and and_1 (S7, \OPERAÇÃO [0], \OPERAÇÃO [1], \OPERAÇÃO [2]);
  and and_2 (S0, not_1_out, not_2_out, not_3_out);
  and and_3 (S1, not_4_out, not_5_out, \OPERAÇÃO [2]);
  and and_4 (S2, not_6_out, \OPERAÇÃO [1], not_7_out);
  and and_5 (S3, not_8_out, \OPERAÇÃO [1], \OPERAÇÃO [2]);
  and and_6 (S4, \OPERAÇÃO [0], not_9_out, not_10_out);
  and and_7 (S5, \OPERAÇÃO [0], not_11_out, \OPERAÇÃO [2]);
  and and_8 (S6, \OPERAÇÃO [0], \OPERAÇÃO [1], not_12_out);
endmodule

module \ROTAÇÃO_À_ESQUERDA  (
  input  [3:0] ABCD,
  input  [1:0] XY,
  output [3:0] abcd_2
);

  wire and_1_out, and_2_out, and_3_out, and_4_out, and_5_out, and_6_out, and_7_out, and_8_out, and_9_out;

  and and_1 (and_1_out, ~XY[1], ~XY[0], ABCD[3]);  // AND_Gate
  and and_2 (and_2_out, ~XY[1], XY[0], ABCD[2]);  // AND_Gate
  and and_3 (and_3_out, XY[1], ~XY[0], ABCD[1]);  // AND_Gate
  and and_4 (and_4_out, XY[1], XY[0], ABCD[0]);
  and and_5 (and_5_out, ~XY[1], ~XY[1], ABCD[2]);  // AND_Gate
  and and_6 (and_6_out, ~XY[1], XY[0], ABCD[1]);  // AND_Gate
  and and_7 (and_7_out, XY[1], ~XY[0], ABCD[0]);  // AND_Gate
  and and_8 (and_8_out, ~XY[1], ~XY[0], ABCD[1]);  // AND_Gate
  and and_9 (and_9_out, ~XY[1], XY[0], ABCD[0]);  // AND_Gate
  and and_10 (abcd_2[0], ~XY[0], ~XY[1], ABCD[0]);  // AND_Gate
  or or_1 (abcd_2[3], and_1_out, and_2_out, and_3_out, and_4_out);
  or or_2 (abcd_2[2], and_5_out, and_6_out, and_7_out);
  or or_3 (abcd_2[1], and_8_out, and_9_out);
endmodule

module \ROTAÇÃO_À_DIREITA  (
  input  [3:0] ABCD,
  input  [1:0] XY,
  output [3:0] abcd_2
);

  wire and_1_out, and_2_out, and_3_out, and_4_out, and_5_out, and_6_out, and_7_out, and_8_out, and_9_out;

  and and_1 (and_1_out, ~XY[1], ~XY[0], ABCD[0]);  // AND_Gate
  and and_2 (and_2_out, ~XY[1], XY[0], ABCD[1]);  // AND_Gate
  and and_3 (and_3_out, XY[1], ~XY[0], ABCD[2]);  // AND_Gate
  and and_4 (and_4_out, XY[1], XY[0], ABCD[3]);
  and and_5 (and_5_out, ~XY[1], ~XY[1], ABCD[1]);  // AND_Gate
  and and_6 (and_6_out, ~XY[1], XY[0], ABCD[2]);  // AND_Gate
  and and_7 (and_7_out, XY[1], ~XY[0], ABCD[3]);  // AND_Gate
  and and_8 (and_8_out, ~XY[1], ~XY[0], ABCD[2]);  // AND_Gate
  and and_9 (and_9_out, ~XY[1], XY[0], ABCD[3]);  // AND_Gate
  and and_10 (abcd_2[3], ~XY[0], ~XY[1], ABCD[3]);  // AND_Gate
  or or_1 (abcd_2[0], and_1_out, and_2_out, and_3_out, and_4_out);
  or or_2 (abcd_2[1], and_5_out, and_6_out, and_7_out);
  or or_3 (abcd_2[2], and_8_out, and_9_out);
endmodule

module OR_4 (
  input  [3:0] B,
  input  [3:0] A,
  output [3:0] S
);

  or or_1 (S[3], A[0], B[3]);
  or or_2 (S[2], A[1], B[1]);
  or or_3 (S[1], A[2], B[2]);
  or or_4 (S[0], A[3], B[0]);
endmodule
